# Fritzing sketch diagramaCompleto (saved by Fritzing 0.9.3b)
breadboards: 1

parts:
  U1 = NodeMCU V3.0
  IC1 = Voltage Regulator [package=to220-igo]
  Batería_Cuadrada = DC Power [voltage=9V]
  R1 = Resistor [tolerance=±5% resistance=100k package=THT]
  R3 = Resistor [tolerance=±5% resistance=68k package=THT]
  U3 = L298 [package=multiwatt15]
  M1 = DC Motor
  M2 = DC Motor
  74LS164 = IC, DIP package, 14 pins [chip_label=74LS164]
  R4 = Resistor [tolerance=±5% resistance=220 package=THT]
  Q1 = PNP-Transistor [package="TO92 [THT]"]
  LED1 = LED - 5mm [color="Red (633nm)" package="5 mm [THT]"]
  R5 = Resistor [tolerance=±5% resistance=220 package=THT]
  LED2 = LED - 5mm [color="Red (633nm)" package="5 mm [THT]"]
  R6 = Resistor [tolerance=±5% resistance=220 package=THT]
  R7 = Resistor [tolerance=±5% resistance=220 package=THT]
  LED3 = LED - 5mm [color="Red (633nm)" package="5 mm [THT]"]
  LED4 = LED - 5mm [color="Red (633nm)" package="5 mm [THT]"]
  LED5 = LED - 5mm [color="Red (633nm)" package="5 mm [THT]"]
  LED6 = LED - 5mm [color="Red (633nm)" package="5 mm [THT]"]
  R8 = Resistor [tolerance=±5% resistance=220 package=THT]
  R9 = Resistor [tolerance=±5% resistance=220 package=THT]
  R10 = Resistor [tolerance=±5% resistance=1k package=THT]
  R11 = Photocell (LDR) [package=THT]
  R12 = Resistor [tolerance=±5% resistance=1k package=THT]
  R13 = Resistor [tolerance=±5% resistance=10k package=THT]
  D1 = Rectifier Diode [part_number=1N4001 package="300 mil [THT]"]
  D2 = Rectifier Diode [part_number=1N4001 package="300 mil [THT]"]
  D3 = Rectifier Diode [part_number=1N4001 package="300 mil [THT]"]
  D4 = Rectifier Diode [part_number=1N4001 package="300 mil [THT]"]
  Pilas_AA = DC Power [voltage=6V]
  U4 = SWITCH_SPDT [package=kps-1290]

nets:
  N1: U1.D0, U3.IN4
  N2: U1.D1, U3.IN3
  N3: U1.D2, U3.IN2
  N4: U1.D3, U3.IN1
  N5: U1.D4, U3.ENA
  N6: U1.3V3, R10.Pin_0, R12.Pin_0
  N7: U1.D5, U3.ENB
  N8: U1.D6, 74LS164.pin1, 74LS164.pin2
  N9: U1.D7, 74LS164.pin8
  N10: U1.D8, Q1.E, R12.Pin_1
  5V: U1.Vin, IC1.OUT, U3.VS, 74LS164.pin14, LED1.anode, LED2.anode, LED3.anode, LED4.anode, LED5.anode, LED6.anode
  GND: U1.GND, IC1.GND, R3.Pin_1, U3.CSA, U3.GND, U3.CSB, 74LS164.pin7, 74LS164.pin9, Q1.C, R13.Pin_1, D3.anode, D4.anode, U4.P
  N11: U1.A0, R1.Pin_1, R3.Pin_0
  N12: IC1.IN, Batería_Cuadrada.V+
  N13: Batería_Cuadrada.V-, Pilas_AA.V-, U4.O
  N14: R1.Pin_0, U3.VLS, D1.cathode, D2.cathode, Pilas_AA.V+
  N15: U3.OUT1, M1.pin_2, D1.anode, D4.cathode
  N16: U3.OUT2, M1.pin_1, D2.anode, D3.cathode
  N17: U3.OUT3, M2.pin_1
  N18: U3.OUT4, M2.pin_2
  N19: 74LS164.pin3, R9.Pin_0
  N20: 74LS164.pin4, R8.Pin_0
  N21: 74LS164.pin5, R7.Pin_0
  N22: 74LS164.pin6, R6.Pin_0
  N23: 74LS164.pin10, R4.Pin_0
  N24: 74LS164.pin11, R5.Pin_0
  N25: R4.Pin_1, LED1.cathode
  N26: Q1.B, R11.pin_1, R13.Pin_0
  N27: R5.Pin_1, LED2.cathode
  N28: R6.Pin_1, LED3.cathode
  N29: R7.Pin_1, LED4.cathode
  N30: LED5.cathode, R8.Pin_1
  N31: LED6.cathode, R9.Pin_1
  N32: R10.Pin_1, R11.pin_0

notes:
  Las líneas cruzadas sin punto no deben conectarse.

custom parts:
  NodeMCU V3.0: ESP8266 based NodeMCU
